# Fritzing sketch AgnesWiring (saved by Fritzing 0.9.3b)
circuit board: 8.46667cm x 5.64444cm

parts:
  Part1 = Arduino Nano (Rev3.0)
  Capacitive_Soil_Moisture_Sensor1 = DFRobot Capacitive Soil Moisture Sensor V1.0 [part_number=SEN0193]
  Capacitive_Soil_Moisture_Sensor2 = DFRobot Capacitive Soil Moisture Sensor V1.0 [part_number=SEN0193]
  U2 = RELAY [package=relay-g5q]
  U3 = RELAY [package=relay-g5q]
  DHT1 = DHT22 Humidity and Temperature Sensor
  Part2 = Adafruit 1.44 inch TFT Breakout [part_number="Adafruit #2088"]

nets:
  GND: Part1.GND, Capacitive_Soil_Moisture_Sensor1.GND, Capacitive_Soil_Moisture_Sensor2.GND, U2.COIL2, U3.COIL2, DHT1.GND, Part2.GND
  N1: Part1.D2, Capacitive_Soil_Moisture_Sensor2.A
  N2: Part1.D3, Capacitive_Soil_Moisture_Sensor1.A
  N3: Part1.D6, U3.COIL1
  N4: Part1.D7, U2.COIL1
  N5: Part1.D8, Part2.TFTDC
  N6: Part1.D9, Part2.RESET
  N7: Part1.D10, Part2.CARDCS
  N8: Part1.D11/MOSI, Part2.MOSI
  VCC: Part1.5V, Capacitive_Soil_Moisture_Sensor1.VCC, Capacitive_Soil_Moisture_Sensor2.VCC, DHT1.VDD, Part2.VIN
  N9: Part1.A2, DHT1.DATA
  N10: Part1.D13/SCK, Part2.SCK

notes:
  Water Level
  Pump
  Light
  Soil

custom parts:
  DFRobot Capacitive Soil Moisture Sensor V1.0: DFRobot Capacitive Soil Moisture Sensor V1.0 This product measures soil moisture levels by capacitive sensing, rather than resistive sensing like other types of moisture sensor. It is made of a corrosion resistant material giving it a long service life. Insert it into soil and impress your friends with the real-time soil moisture data! The product includes an on-board voltage regulator which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
  Adafruit 1.44 inch TFT Breakout: This lovely little display breakout is the best way to add a small, colorful and bright display to any project. Since the display uses 4-wire SPI to communicate and has its own pixel-addressable frame buffer, it can be used with every kind of microcontroller. Even a very small one with low memory and few pins available! The 1.44" display has 128x128 color pixels. Unlike the low cost "Nokia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
